// Logisim project A or S selector.circ as structural Verilog: 1 circuit, main circuit Final selector
module Final_selector (
  input  Sign_A,
  input  Sign_B,
  input  OP,
  output out_4
);

  wire n7486_1_p3;

  // _7486 7486_1: pin names not known; wires that end beside it: Sign_A, Sign_B, n7486_1_p3, n7486_1_p3, OP, out_4
endmodule
