// Logisim project Add & subtract.circ as structural Verilog: 1 circuit, main circuit main
module main (
  input  OP0,
  input  A0,
  input  A1,
  input  SignA,
  input  B0,
  input  B1,
  input  SignB,
  output Sub0,
  output Sub1,
  output Sub_Sign,
  output Add_sign,
  output Add2,
  output Add1,
  output Add0
);

  wire Sign_Check_s_selector, Sub_Selector__1out0, Sub_Selector__1out1, Sub_Selector_out0, Sub_Selector_out1;

  Sign_Check Sign_Check (
    .SignA(SignA), .Op0(OP0), .SignB(SignB), .A_sign(Add_sign), .S_selector(Sign_Check_s_selector));
  Sub_Selector Sub_Selector (
    .S(Sign_Check_s_selector), .A0(A0), .A1(A1), .B0(B0), .B1(B1), ._1OUT1(Sub_Selector__1out1),
    ._1OUT0(Sub_Selector__1out0), .OUT1(Sub_Selector_out1), .OUT0(Sub_Selector_out0));
  Subtraction_main Subtract (
    .A0(Sub_Selector__1out0), .A1(Sub_Selector__1out1), .B0(Sub_Selector_out0), .B1(Sub_Selector_out1),
    .Out0(Sub0), .Out1(Sub1), .Out2(Sub_Sign));
  Final_Addition Addition (.B0(B0), .A0(A0), .B1(B1), .A1(A1), .S2(Add2), .S1(Add1), .S0(Add0));
endmodule
