// Logisim project Addition.circ as structural Verilog: 1 circuit, main circuit Final Addition
module Final_Addition (
  input  B0,
  input  A0,
  input  B1,
  input  A1,
  output S2,
  output S1,
  output S0
);

  // _7483 7483_1: pin names not known; wires that end beside it: 1'b0, S2, 1'b0, 1'b0, 1'b1, S1, B1, A1, 1'b0, 1'b0, 1'b0, 1'b0, B0, A0, S0
endmodule
