// Logisim project Answer.circ as structural Verilog: 1 circuit, main circuit Answer
module Answer (
  input  OP0,
  input  OP1,
  input  A0___S0,
  input  M0,
  input  R0,
  input  A1___S1,
  input  M1,
  input  R1,
  input  A2___S2,
  input  M2,
  input  M3,
  input  Sign_A___Sign_b,
  input  Sign_M,
  input  Sign_R,
  output _0,
  output _1,
  output _2,
  output _3,
  output SIGN
);

  // _74153 74153_1: pin names not known; wires that end beside it: 1'b0, OP1, 1'b0, M2, A2___S2, A2___S2, _2, 1'b0, 1'b0, OP0, 1'b0, M3, 1'b0, 1'b0, _3
  // _74153 74153_2: pin names not known; wires that end beside it: 1'b0, OP1, Sign_R, Sign_M, Sign_A___Sign_b, Sign_A___Sign_b, SIGN, 1'b0, OP0
  // _74153 74153_3: pin names not known; wires that end beside it: 1'b0, OP1, R0, M0, A0___S0, A0___S0, _0, 1'b0, 1'b0, OP0, R1, M1, A1___S1, A1___S1, _1
endmodule
