// Logisim project Display.circ as structural Verilog: 1 circuit, main circuit main
module main (
  input  OP0,
  input  OP1,
  input  A0,
  input  A1,
  input  A2,
  input  B0,
  input  B1,
  input  B2
);

  wire ALU__0, ALU__1, ALU__2, ALU__3, ALU_devide_zero_flag, ALU_sign, Divide_By_Zero_buzzer,
       n7_segment_display_driver_1_p5, n7_segment_display_driver_1_p6, n7_segment_display_driver_1_p7,
       n7_segment_display_driver_1_p8, n7_segment_display_driver_1_p9, n7_segment_display_driver_1_p10,
       n7_segment_display_driver_1_p11, n7425_1_p5;

  Final_circuit_main ALU (
    .OP0(OP0), .OP1(OP1), .A0(A0), .A1(A1), .A2(A2), .B0(B0), .B1(B1), .B2(B2), ._0(ALU__0), ._1(ALU__1),
    ._2(ALU__2), ._3(ALU__3), .Sign(ALU_sign), .Devide_Zero_Flag(ALU_devide_zero_flag));
  Divide_by_zero_main Divide_By_Zero (
    .OP0(OP0), .OP1(OP1), .Divide_Zero(ALU_devide_zero_flag), .Buzzer(Divide_By_Zero_buzzer));
  // _7425 7425_1: pin names not known; wires that end beside it: ALU__0, ALU__1, ALU__2, ALU__3, n7425_1_p5, 1'b0, 1'b1
  // _7_segment_display_driver 7_segment_display_driver_1: pin names not known; wires that end beside it: ALU__3, ALU__2, ALU__1, ALU__0, n7_segment_display_driver_1_p5, n7_segment_display_driver_1_p6, n7_segment_display_driver_1_p7, n7_segment_display_driver_1_p8, n7_segment_display_driver_1_p9, n7_segment_display_driver_1_p10, n7_segment_display_driver_1_p11
  _7_Segment_Display u_7_segment_display_1 (.g(ALU_sign));  // open: f, a, b, e, d, c, dp
  LED Sign_Flag (.in(ALU_sign));
  LED Zero_Flag (.in(n7425_1_p5));
  LED Buzzer (.in(Divide_By_Zero_buzzer));
  _7_Segment_Display u_7_segment_display_2 (
    .g(n7_segment_display_driver_1_p11), .f(n7_segment_display_driver_1_p10),
    .a(n7_segment_display_driver_1_p5), .b(n7_segment_display_driver_1_p6),
    .e(n7_segment_display_driver_1_p9), .d(n7_segment_display_driver_1_p8), .c(n7_segment_display_driver_1_p7));  // open: dp

  // Notes on the sheet:
  //   Omar Ashraf Mabrouk 1200036 (Addition & Subtraction)
  //   Ahmed Mohamed Helmy 120097 (Addition & Subtraction)
  //   Omar Ehab Mohamed 1200037 (Multiplication)
  //   Ahmed Maged Mahmoud 1200014 (Remainder)
  //   00 Adition
  //   01 Subtraction
  //   10 Multiplication
  //   11 Remainder
endmodule
