// Logisim project Divide by zero.circ as structural Verilog: 1 circuit, main circuit main
module main (
  input  OP0,
  input  OP1,
  input  Divide_Zero,
  output Buzzer
);

  wire n7408_1_p3;

  // _7408 7408_1: pin names not known; wires that end beside it: OP0, OP1, n7408_1_p3, n7408_1_p3, Divide_Zero, Buzzer, 1'b0, 1'b1
endmodule
