// Logisim project Division.circ as structural Verilog: 1 circuit, main circuit main
module main (
  input  A0,
  input  A1,
  input  A2,
  input  B0,
  input  B1,
  output R_sign,
  output Devide_Zero_Flag,
  output R1,
  output R0
);

  wire n7404_1_p2, n7404_1_p4, n7404_1_p6, n7404_1_p8, n7408_1_p6, n7408_1_p9, n7408_2_p3, n7408_2_p5;

  // _7404 7404_1: pin names not known; wires that end beside it: B1, n7404_1_p2, B0, n7404_1_p4, A0, n7404_1_p6, A1, n7404_1_p8
  // _7408 7408_1: pin names not known; wires that end beside it: n7404_1_p2, n7404_1_p4, Devide_Zero_Flag, A1, n7404_1_p6, n7408_1_p6, n7408_1_p6, B1, n7408_1_p9, n7408_1_p9, B0, R1
  // _7408 7408_2: pin names not known; wires that end beside it: A0, B1, n7408_2_p3, n7408_2_p3, n7408_2_p5, R0
  // _7432 7432_1: pin names not known; wires that end beside it: n7404_1_p8, n7404_1_p4, n7408_2_p5

  assign R_sign = A2;
endmodule
