// Logisim project Final circuit.circ as structural Verilog: 1 circuit, main circuit main
module main (
  input  OP0,
  input  OP1,
  input  A0,
  input  A1,
  input  A2,
  input  B0,
  input  B1,
  input  B2,
  output _0,
  output _1,
  output _2,
  output _3,
  output Sign,
  output Devide_Zero_Flag
);

  wire A_S_add0, A_S_add1, A_S_add2, A_S_add_sign, A_S_sub0, A_S_sub1, A_S_sub_sign, M_m0, M_m1, M_m2, M_m3,
       M_m_sign, Out_A_or_S_a0_or_s0, Out_A_or_S_a1_or_s1, Out_A_or_S_a2_or_0, Out_A_or_S_sign_a_or_sign_s,
       R_r0, R_r1, R_r_sign, Select_A_or_S_out_4;

  Final_selector Select_A_or_S (.Sign_A(A2), .Sign_B(B2), .OP(OP0), .out_4(Select_A_or_S_out_4));
  Add___subtract_main A_S (
    .OP0(OP0), .A0(A0), .A1(A1), .SignA(A2), .B0(B0), .B1(B1), .SignB(B2), .Sub0(A_S_sub0), .Sub1(A_S_sub1),
    .Sub_Sign(A_S_sub_sign), .Add_sign(A_S_add_sign), .Add2(A_S_add2), .Add1(A_S_add1), .Add0(A_S_add0));
  Multiplication M (
    .A0(A0), .A1(A1), .A2(A2), .B0(B0), .B1(B1), .B2(B2), .M0(M_m0), .M1(M_m1), .M2(M_m2), .M3(M_m3),
    .M_sign(M_m_sign));
  Division_main R (
    .A0(A0), .A1(A1), .A2(A2), .B0(B0), .B1(B1), .R_sign(R_r_sign), .Devide_Zero_Flag(Devide_Zero_Flag),
    .R1(R_r1), .R0(R_r0));
  Out_A_or_S Out_A_or_S (
    .Selector(Select_A_or_S_out_4), .S0(A_S_sub0), .S1(A_S_sub1), .Sign_S(A_S_sub_sign), .A0(A_S_add0),
    .A1(A_S_add1), .A2(A_S_add2), .Sign_A(A_S_add_sign), .Sign_A_or_Sign_S(Out_A_or_S_sign_a_or_sign_s),
    .A2_or_0(Out_A_or_S_a2_or_0), .A1_or_S1(Out_A_or_S_a1_or_s1), .A0_or_S0(Out_A_or_S_a0_or_s0));
  Answer Answer (
    .OP0(OP0), .OP1(OP1), .A0___S0(Out_A_or_S_a0_or_s0), .M0(M_m0), .R0(R_r0), .A1___S1(Out_A_or_S_a1_or_s1),
    .M1(M_m1), .R1(R_r1), .A2___S2(Out_A_or_S_a2_or_0), .M2(M_m2), .M3(M_m3),
    .Sign_A___Sign_b(Out_A_or_S_sign_a_or_sign_s), .Sign_M(M_m_sign), .Sign_R(R_r_sign), ._0(_0), ._1(_1),
    ._2(_2), ._3(_3), .SIGN(Sign));

  // Notes on the sheet:
  //   00 Add
  //   01 Subtraction
  //   10 Multiplication
  //   11 Remainder
  //   Devide Zero Flag 
  //   S0
  //   S1
  //   Sign S
  //   A0
  //   A1
  //   A2
  //   Sign A
  //   M0
  //   M1
  //   M2
  //   M3
  //   Sign M
  //   Sign R
  //   R1
  //   R0
  //   If 0 then addition if 1 then subtraction
endmodule
