// Logisim project Multiplication.circ as structural Verilog: 1 circuit, main circuit Multiplication
module Multiplication (
  input  A0,
  input  A1,
  input  A2,
  input  B0,
  input  B1,
  input  B2,
  output M0,
  output M1,
  output M2,
  output M3,
  output M_sign
);

  wire n7408_1_p6, n7408_1_p11, n7408_1_p14;

  // _7486 7486_1: pin names not known; wires that end beside it: A2, B2, M_sign, 1'b0, 1'b1
  // _7408 7408_1: pin names not known; wires that end beside it: A0, B0, M0, A1, B0, n7408_1_p6, 1'b0, 1'b1, B1, A0, n7408_1_p11, B1, A1, n7408_1_p14
  Final_Addition Addition (.B0(n7408_1_p11), .A0(n7408_1_p6), .B1(n7408_1_p14), .A1(1'b0), .S2(M3), .S1(M2), .S0(M1));
endmodule
