// Logisim project Out A or S.circ as structural Verilog: 1 circuit, main circuit Out A or S
module Out_A_or_S (
  input  Selector,
  input  S0,
  input  S1,
  input  Sign_S,
  input  A0,
  input  A1,
  input  A2,
  input  Sign_A,
  output Sign_A_or_Sign_S,
  output A2_or_0,
  output A1_or_S1,
  output A0_or_S0
);

  // _74157 74157_1: pin names not known; wires that end beside it: Selector, A0, S0, A0_or_S0, A1, S1, A1_or_S1, 1'b0, 1'b1, 1'b0, Sign_A, Sign_S, Sign_A_or_Sign_S, A2, 1'b0, A2_or_0
endmodule
