// Logisim project Sign Check.circ as structural Verilog: 1 circuit, main circuit Sign Check
module Sign_Check (
  input  SignA,
  input  Op0,
  input  SignB,
  output A_sign,
  output S_selector
);

  wire n7404_1_p2, n7486_1_p3;

  // _7486 7486_1: pin names not known; wires that end beside it: Op0, SignB, n7486_1_p3, 1'b0, 1'b0, 1'b1
  // _7404 7404_1: pin names not known; wires that end beside it: SignA, n7404_1_p2, 1'b1
  // _7408 7408_1: pin names not known; wires that end beside it: n7404_1_p2, n7486_1_p3, S_selector, SignA, n7486_1_p3, A_sign, 1'b0, 1'b1
endmodule
