// Logisim project Sub Selector.circ as structural Verilog: 1 circuit, main circuit Sub Selector
module Sub_Selector (
  input  S,
  input  A0,
  input  A1,
  input  B0,
  input  B1,
  output _1OUT1,
  output _1OUT0,
  output OUT1,
  output OUT0
);

  // _74157 74157_1: pin names not known; wires that end beside it: S, A0, B0, OUT0, A1, B1, OUT1, 1'b0, 1'b1, 1'b0, B1, A1, _1OUT1, B0, A0, _1OUT0
endmodule
