// Logisim project Subtraction.circ as structural Verilog: 1 circuit, main circuit main
module main (
  input  A0,
  input  A1,
  input  B0,
  input  B1,
  output Out0,
  output Out1,
  output Out2
);

  wire n7404_1_p2, n7404_1_p4, n7404_1_p5, n7404_1_p6, n7404_1_p9, n7404_1_p11, n7404_1_p12, n7408_1_p3,
       n7408_1_p6, n7408_1_p11, n7408_1_p14, n7408_2_p3, n7408_2_p6, n7432_1_p3;

  // _7404 7404_1: pin names not known; wires that end beside it: B0, n7404_1_p2, B1, n7404_1_p4, n7404_1_p5, n7404_1_p6, 1'b0, 1'b1, n7404_1_p9, Out0, n7404_1_p11, n7404_1_p12
  Final_Addition Addition (
    .B0(n7404_1_p2), .A0(A0), .B1(n7404_1_p4), .A1(A1), .S2(n7404_1_p5), .S1(n7404_1_p11), .S0(n7404_1_p9));
  // _7408 7408_1: pin names not known; wires that end beside it: n7404_1_p6, n7404_1_p12, n7408_1_p3, n7404_1_p12, n7404_1_p9, n7408_1_p6, 1'b0, 1'b1, n7404_1_p5, n7404_1_p11, n7408_1_p11, n7408_1_p11, Out0, n7408_1_p14
  // _7408 7408_2: pin names not known; wires that end beside it: n7404_1_p6, Out0, n7408_2_p3, n7404_1_p6, n7404_1_p12, n7408_2_p6, 1'b0, 1'b1
  // _7432 7432_1: pin names not known; wires that end beside it: n7408_1_p3, n7408_1_p6, n7432_1_p3, n7432_1_p3, n7408_1_p14, Out1, 1'b0, 1'b1, n7408_2_p3, n7408_2_p6, Out2
endmodule
